// Logisim project ULA.circ as structural Verilog: 1 circuit, main circuit ULA
module ULA (
  input  [3:0] IMEDIATO_000,
  input  [3:0] ENTRADA_Y,
  input  [3:0] ENTRADA_X,
  input  S1,
  input  S0,
  output [3:0] RESULTADO_OP,
  output EQUAL
);

  wire [3:0] multiplicador_1_s, soma_4_bits_1_s, \subtraçao_4_bits_1_s ;

  Soma_4_Bits soma_4_bits_1 (.Y(ENTRADA_Y), .X(ENTRADA_X), .S(soma_4_bits_1_s));  // open: Carry
  \Subtraçao_4_Bits  \subtraçao_4_bits_1  (.Y(ENTRADA_Y), .X(ENTRADA_X), .S(\subtraçao_4_bits_1_s ));  // open: Bout
  multiplicador multiplicador_1 (.Y(ENTRADA_Y), .S(multiplicador_1_s), .X(ENTRADA_X));
  comparador_main main_1 (.Y(ENTRADA_Y), .X(ENTRADA_X), .out_3(EQUAL));  // open: out_5, out_4
  MUX4B mux4b_1 (
    .SUM__00(IMEDIATO_000), .SUB__01(soma_4_bits_1_s), .MUL__10(\subtraçao_4_bits_1_s ), .S1(S1), .S0(S0),
    .Out(RESULTADO_OP), .CMP__11(multiplicador_1_s));
endmodule
