// Logisim project comparador.circ as structural Verilog: 1 circuit, main circuit main
module main (
  input  [3:0] Y,
  input  [3:0] X,
  output out_3,
  output out_4,
  output out_5
);

  wire and_1_out, and_2_out, and_3_out, and_4_out, and_5_out, and_6_out, and_7_out, and_9_out, and_10_out,
       and_11_out, not_1_out, not_2_out, not_3_out, not_4_out, not_5_out, not_6_out, not_7_out, not_8_out,
       not_9_out, not_10_out, not_11_out, not_12_out, xnor_1_out, xnor_2_out, xnor_3_out, xnor_4_out;

  xnor xnor_1 (xnor_1_out, Y[0], X[0]);
  xnor xnor_2 (xnor_2_out, Y[1], X[1]);
  xnor xnor_3 (xnor_3_out, Y[2], X[2]);
  xnor xnor_4 (xnor_4_out, Y[3], X[3]);
  not not_1 (not_1_out, xnor_4_out);
  not not_2 (not_2_out, Y[3]);
  not not_3 (not_3_out, X[3]);
  and and_1 (and_1_out, xnor_1_out, xnor_2_out);
  and and_2 (and_2_out, xnor_3_out, xnor_4_out);
  and and_3 (and_3_out, not_1_out, not_2_out, X[3]);
  not not_4 (not_4_out, xnor_3_out);
  not not_5 (not_5_out, Y[2]);
  not not_6 (not_6_out, xnor_2_out);
  not not_7 (not_7_out, Y[1]);
  not not_8 (not_8_out, X[2]);
  and and_4 (and_4_out, not_1_out, Y[3], not_3_out);
  and and_5 (and_5_out, not_4_out, not_5_out, X[2]);
  and and_6 (and_6_out, not_6_out, not_7_out, X[1]);
  not not_9 (not_9_out, xnor_1_out);
  not not_10 (not_10_out, Y[0]);
  not not_11 (not_11_out, X[0]);
  not not_12 (not_12_out, X[1]);
  and and_7 (and_7_out, not_4_out, Y[2], not_8_out);
  and and_8 (out_3, and_1_out, and_2_out);
  and and_9 (and_9_out, not_9_out, not_10_out, X[0]);
  and and_10 (and_10_out, not_9_out, Y[0], not_11_out);
  and and_11 (and_11_out, not_6_out, Y[0], not_12_out);
  or or_1 (out_4, and_3_out, and_6_out, and_9_out, and_5_out);
  or or_2 (out_5, and_10_out, and_11_out, and_7_out, and_4_out);

  // Notes on the sheet:
  //   VERIFICA SE X= Y
  //   VERIFICA SE X > Y
  //   VERIFICA SE X < Y
endmodule
