// Logisim project controle.circ as structural Verilog: 1 circuit, main circuit Controle
module Controle (
  input  Reset,
  input  Clock,
  input  OPCODE_2,
  input  OPCODE_1,
  input  OPCODE_0,
  input  Equal,
  output Out_WRITE,
  output Out_EN_PC,
  output Out_LOAD,
  output STORE
);

  wire and_1_out, and_2_out, and_3_out, and_4_out, EN_BEQ_out, EN_BNE_out, EN_JMP_out, not_1_out, not_2_out,
       not_3_out, not_4_out, not_5_out, or_1_out, ST0_q, ST0_qn, ST1_q, ST1_qn;

  and and_1 (and_1_out, OPCODE_2, OPCODE_0, OPCODE_1);
  not not_1 (not_1_out, OPCODE_2);
  and and_2 (and_2_out, ST1_qn, OPCODE_2, ST0_qn);
  and and_3 (and_3_out, ST1_qn, and_1_out, ST0_qn);
  and and_4 (and_4_out, ST1_qn, not_1_out, ST0_qn);
  or or_1 (or_1_out, and_3_out, and_4_out);
  not not_2 (not_2_out, OPCODE_0);
  not not_3 (not_3_out, OPCODE_0);
  D_Flip_Flop ST1 (.clk(Clock), .D(and_2_out), .Q(ST1_q), .Qn(ST1_qn), .reset(Reset));  // open: preset, en
  not not_4 (not_4_out, OPCODE_1);
  not not_5 (not_5_out, Equal);
  and EN_JMP (EN_JMP_out, OPCODE_2, ST0_qn, not_2_out, not_4_out);
  and EN_BEQ (EN_BEQ_out, OPCODE_1, ST0_qn, Equal, not_3_out, OPCODE_2);
  and EN_BNE (EN_BNE_out, not_5_out, not_4_out, OPCODE_2, ST0_qn, OPCODE_1);
  and and_5 (STORE, ST1_q, ST0_q);
  D_Flip_Flop ST0 (.clk(Clock), .D(or_1_out), .Q(ST0_q), .Qn(ST0_qn), .reset(Reset));  // open: preset, en
  or or_2 (Out_EN_PC, ST1_q, ST0_q);
  or or_3 (Out_LOAD, EN_JMP_out, EN_BEQ_out, EN_BNE_out);
  and and_6 (Out_WRITE, ST1_qn, ST0_q);
endmodule
