// Logisim project FA.circ as structural Verilog: 1 circuit, main circuit FA
module FA (
  input  Cin,
  input  X,
  input  Y,
  output S,
  output Cout
);

  wire ha_1_carry, ha_1_s, ha_2_carry;

  HA ha_1 (.X(X), .Y(Y), .Carry(ha_1_carry), .S(ha_1_s));
  HA ha_2 (.X(Cin), .Y(ha_1_s), .Carry(ha_2_carry), .S(S));
  or or_1 (Cout, ha_2_carry, ha_1_carry);
endmodule
