// Logisim project HA.circ as structural Verilog: 1 circuit, main circuit HA
module HA (
  input  X,
  input  Y,
  output S,
  output Carry
);

  and and_1 (Carry, X, Y);
  xor xor_1 (S, X, Y);
endmodule
