// Logisim project mini-arquitetura.circ as structural Verilog: 1 circuit, main circuit mini-arquitetura
module mini_arquitetura (
  input  RESET,
  output [2:0] RD,
  output [3:0] REG0,
  output [2:0] OPCODE,
  output [3:0] REG1,
  output [3:0] REG2,
  output [3:0] REG3,
  output [3:0] REG4,
  output [3:0] REG5,
  output [3:0] REG6,
  output [3:0] REG7,
  output [2:0] RF1,
  output [2:0] RF2
);

  wire clock_1_out, controle_1_out_en_pc, controle_1_out_load, controle_1_out_write, controle_1_store,
       decodificador_1_d0, decodificador_1_d1, decodificador_1_d2, decodificador_1_d3, decodificador_1_d4,
       decodificador_1_d5, decodificador_1_d6, decodificador_1_d7, ula_1_equal;
  wire [3:0] main_1_out_6, multiplexer_1_out, multiplexer_2_out, ram_2_data, ula_1_resultado_op;

  Clock clock_1 (.out(clock_1_out));
  contador_main main_1 (
    .RESET(RESET), .LOAD(controle_1_out_load), .DATA(ram_2_data), .out_6(main_1_out_6), .CLOCK(clock_1_out),
    .ENABLE(controle_1_out_en_pc));
  RAM #(.addrWidth(4), .dataWidth(4), .bus("separate")) ram_1 (
    .addr(ram_2_data), .din(multiplexer_1_out), .str(1'b1), .sel(controle_1_store), .clk(clock_1_out));  // open: data, ld, clr
  RAM #(.addrWidth(4), .dataWidth(16)) ram_2 (
    .addr(main_1_out_6), .data({OPCODE, RD, RF1, RF2, ram_2_data}), .clk(clock_1_out));  // open: sel, ld, clr
  ULA ula_1 (
    .IMEDIATO_000(ram_2_data), .ENTRADA_Y(multiplexer_2_out), .ENTRADA_X(multiplexer_1_out), .S1(OPCODE[1]),
    .S0(OPCODE[0]), .RESULTADO_OP(ula_1_resultado_op), .EQUAL(ula_1_equal));
  DECODIFICADOR decodificador_1 (
    .SELECT(RD), .D0(decodificador_1_d0), .D1(decodificador_1_d1), .D2(decodificador_1_d2),
    .D3(decodificador_1_d3), .D4(decodificador_1_d4), .D5(decodificador_1_d5), .D6(decodificador_1_d6),
    .D7(decodificador_1_d7));
  Multiplexer #(.select(3), .width(4)) multiplexer_1 (
    .in0(REG0), .in1(REG1), .in2(REG2), .in3(REG3), .in4(REG4), .in5(REG5), .in6(REG6), .in7(REG7),
    .out(multiplexer_1_out), .sel(RF1));  // open: en
  Multiplexer #(.select(3), .width(4)) multiplexer_2 (
    .in0(REG0), .in1(REG1), .in2(REG2), .in3(REG3), .in4(REG4), .in5(REG5), .in6(REG6), .in7(REG7),
    .out(multiplexer_2_out), .sel(RF2));  // open: en
  Controle controle_1 (
    .Reset(RESET), .Clock(clock_1_out), .OPCODE_2(OPCODE[2]), .OPCODE_1(OPCODE[1]), .OPCODE_0(OPCODE[0]),
    .Equal(ula_1_equal), .Out_WRITE(controle_1_out_write), .Out_LOAD(controle_1_out_load),
    .Out_EN_PC(controle_1_out_en_pc), .STORE(controle_1_store));
  banco_registradores_main main_2 (
    .Reset(RESET), .En_Reg0(decodificador_1_d0), .En_Reg1(decodificador_1_d1), .En_Reg2(decodificador_1_d2),
    .En_Reg3(decodificador_1_d3), .DATA(ula_1_resultado_op), .En_Reg4(decodificador_1_d4),
    .En_Reg5(decodificador_1_d5), .En_Reg6(decodificador_1_d6), .En_Reg_7(decodificador_1_d7),
    .Clock(clock_1_out), .Out_Reg0(REG0), .Out_Reg1(REG1), .Out_Reg2(REG2), .Out_Reg3(REG3), .Out_Reg4(REG4),
    .Out_Reg5(REG5), .Out_Reg6(REG6), .Out_Reg7(REG7), .WRITE(controle_1_out_write));
endmodule
