// Logisim project multiplicador.circ as structural Verilog: 1 circuit, main circuit multiplicador
module multiplicador (
  input  [3:0] Y,
  input  [3:0] X,
  output [3:0] S
);

  wire fa_1_cout, fa_1_s, fa_2_cout, fa_2_s, fa_3_cout, fa_3_s, fa_4_cout, fa_4_s, fa_5_cout, fa_5_s,
       fa_6_cout, fa_6_s, fa_7_cout, fa_7_s, fa_8_cout, fa_8_s, ha_1_carry, ha_1_s, ha_2_carry, ha_3_carry,
       ha_4_carry, X0Y1_out, X0Y2_out, X0Y3_out, X1Y0_out, X1Y1_out, X1Y2_out, X1Y3_out, X2Y0_out, X2Y1_out,
       X2Y2_out, X2Y3_out, X3Y0_out, X3Y1_out, X3Y2_out, X3Y3_out;

  and X3Y3 (X3Y3_out, X[3], Y[3]);
  and X3Y1 (X3Y1_out, X[3], Y[1]);
  and X3Y2 (X3Y2_out, X[3], Y[2]);
  FA fa_1 (.Cin(fa_2_cout), .X(ha_1_carry), .Y(X3Y2_out), .S(fa_1_s), .Cout(fa_1_cout));
  HA ha_1 (.X(fa_4_cout), .Y(X3Y1_out), .Carry(ha_1_carry), .S(ha_1_s));
  and X2Y2 (X2Y2_out, X[2], Y[2]);
  FA fa_2 (.Cin(fa_7_cout), .X(X2Y2_out), .Y(ha_1_s), .S(fa_2_s), .Cout(fa_2_cout));
  and X2Y3 (X2Y3_out, X[2], Y[3]);
  FA fa_3 (.Cin(fa_5_cout), .X(X3Y3_out), .Y(fa_1_cout), .S(fa_3_s), .Cout(fa_3_cout));
  and X3Y0 (X3Y0_out, X[3], Y[0]);
  and X2Y1 (X2Y1_out, X[2], Y[1]);
  FA fa_4 (.Cin(fa_6_cout), .X(X2Y1_out), .Y(X3Y0_out), .S(fa_4_s), .Cout(fa_4_cout));
  and X1Y2 (X1Y2_out, X[1], Y[2]);
  and X1Y3 (X1Y3_out, X[2], Y[3]);
  FA fa_5 (.Cin(fa_8_cout), .X(fa_1_s), .Y(X2Y3_out), .S(fa_5_s), .Cout(fa_5_cout));
  and X2Y0 (X2Y0_out, X[2], Y[0]);
  and X1Y1 (X1Y1_out, X[1], Y[1]);
  FA fa_6 (.Cin(ha_4_carry), .X(X1Y1_out), .Y(X2Y0_out), .S(fa_6_s), .Cout(fa_6_cout));
  FA fa_7 (.Cin(ha_2_carry), .X(X1Y2_out), .Y(fa_4_s), .S(fa_7_s), .Cout(fa_7_cout));
  FA fa_8 (.Cin(ha_3_carry), .X(fa_2_s), .Y(X1Y3_out), .S(fa_8_s), .Cout(fa_8_cout));
  and X1Y0 (X1Y0_out, X[1], Y[0]);
  and X0Y2 (X0Y2_out, X[0], Y[2]);
  HA ha_2 (.X(X0Y2_out), .Y(fa_6_s), .Carry(ha_2_carry), .S(S[2]));
  HA ha_3 (.X(X0Y3_out), .Y(fa_7_s), .Carry(ha_3_carry), .S(S[3]));
  and X0Y1 (X0Y1_out, X[0], Y[1]);
  HA ha_4 (.X(X0Y1_out), .Y(X1Y0_out), .Carry(ha_4_carry), .S(S[1]));
  and X0Y3 (X0Y3_out, X[0], Y[3]);
  and X0Y0 (S[0], X[0], Y[0]);
endmodule
