// Logisim project mux_4bit.circ as structural Verilog: 1 circuit, main circuit MUX4B
module MUX4B (
  input  [3:0] SUM__00,
  input  [3:0] SUB__01,
  input  [3:0] MUL__10,
  input  [3:0] CMP__11,
  input  S1,
  input  S0,
  output [3:0] Out
);

  MUX mux_1 (.S1(S1), .S0(S0), .D0(SUM__00[0]), .D1(SUB__01[0]), .D2(MUL__10[0]), .D3(CMP__11[0]), .out_7(Out[0]));
  MUX mux_2 (.S1(S1), .S0(S0), .D0(SUM__00[1]), .D1(SUB__01[1]), .D2(MUL__10[1]), .D3(CMP__11[1]), .out_7(Out[1]));
  MUX mux_3 (.S1(S1), .S0(S0), .D0(SUM__00[2]), .D1(SUB__01[2]), .D2(MUL__10[2]), .D3(CMP__11[2]), .out_7(Out[2]));
  MUX mux_4 (.S1(S1), .S0(S0), .D0(SUM__00[3]), .D1(SUB__01[3]), .D2(MUL__10[3]), .D3(CMP__11[3]), .out_7(Out[3]));
endmodule
