// Logisim project FSM.circ as structural Verilog: 1 circuit, main circuit main
module main (
  input  RESET,
  input  OP,
  input  [3:0] ENTRADA_1,
  input  WB,
  input  [3:0] ENTRADA_2
);

  wire and_1_out, and_2_out, and_3_out, and_4_out, and_5_out, and_6_out, and_7_out, and_8_out, and_9_out,
       and_10_out, and_11_out, and_12_out, clock_1_out, not_1_out, not_2_out, not_3_out, not_4_out,
       not_5_out, not_6_out, not_7_out, or_1_out, or_2_out, or_3_out, or_4_out, or_5_out, or_6_out, ST0_q,
       ST0_qn, ST1_q, ST1_qn;
  wire [3:0] multiplexer_1_out, multiplexer_2_out, REG_A_q, REG_B_q, register_1_q, sum_sub_1_s;

  Clock clock_1 (.out(clock_1_out));
  J_K_Flip_Flop ST0 (
    .J(or_4_out), .clk(clock_1_out), .K(or_5_out), .Q(ST0_q), .Qn(ST0_qn), .reset(RESET));  // open: preset, en
  J_K_Flip_Flop ST1 (
    .J(or_1_out), .clk(clock_1_out), .K(or_2_out), .Q(ST1_q), .Qn(ST1_qn), .reset(RESET));  // open: preset, en
  and and_1 (and_1_out, OP, ST0_qn);
  and and_2 (and_2_out, ST0_q, WB);
  and and_3 (and_3_out, ST0_q, not_1_out);
  not not_1 (not_1_out, OP);
  and and_4 (and_4_out, ST0_qn, not_2_out);
  not not_2 (not_2_out, WB);
  and and_5 (and_5_out, ST1_qn, ST0_qn);
  not not_3 (not_3_out, ST1_qn);
  and and_6 (and_6_out, not_3_out, not_4_out);
  not not_4 (not_4_out, ST0_qn);
  not not_5 (not_5_out, OP);
  or or_1 (or_1_out, and_1_out, and_2_out);
  or or_2 (or_2_out, and_3_out, and_4_out);
  or or_3 (or_3_out, and_5_out, and_6_out);
  and and_7 (and_7_out, ST1_q, WB);
  and and_8 (and_8_out, not_5_out, ST1_qn);
  and and_9 (and_9_out, ST1_qn, not_2_out);
  not not_6 (not_6_out, ST1_qn);
  and and_10 (and_10_out, not_6_out, OP);
  not not_7 (not_7_out, ST1_qn);
  or or_4 (or_4_out, and_7_out, and_8_out);
  or or_5 (or_5_out, and_9_out, and_10_out);
  and and_11 (and_11_out, not_7_out, ST0_qn);
  and and_12 (and_12_out, ST0_q, ST1_qn);
  or or_6 (or_6_out, and_12_out, and_11_out);
  Multiplexer #(.width(4)) multiplexer_1 (
    .in0(REG_A_q), .in1(ENTRADA_2), .out(multiplexer_1_out), .sel(ST0_qn));  // open: en
  Multiplexer #(.width(4)) multiplexer_2 (
    .in0(register_1_q), .in1(ENTRADA_1), .out(multiplexer_2_out), .sel(ST0_qn));  // open: en
  Register #(.width(4)) REG_A (.D(multiplexer_2_out), .en(or_3_out), .Q(REG_A_q), .clk(clock_1_out), .clr(RESET));
  Register #(.width(4)) REG_B (.D(multiplexer_1_out), .en(or_3_out), .Q(REG_B_q), .clk(clock_1_out), .clr(RESET));
  SUM_SUB sum_sub_1 (.Y(REG_B_q), .X(REG_A_q), .S(sum_sub_1_s), .M__SUM_0___SUB_1(ST0_qn));  // open: Carry
  Register #(.width(4)) register_1 (.D(sum_sub_1_s), .en(or_6_out), .Q(register_1_q), .clk(clock_1_out), .clr(RESET));
endmodule
