// Logisim project SUB.circ as structural Verilog: 1 circuit, main circuit Subtraçao 4 Bits
module \Subtraçao_4_Bits  (
  input  [3:0] Y,
  input  [3:0] X,
  output Bout,
  output [3:0] S
);

  wire fa_1_cout, fa_2_cout, fa_3_cout, xor_1_out, xor_2_out, xor_3_out, xor_4_out;

  xor xor_1 (xor_1_out, Y[3], 1'b1);
  xor xor_2 (xor_2_out, 1'b1, Y[0]);
  xor xor_3 (xor_3_out, Y[1], 1'b1);
  xor xor_4 (xor_4_out, Y[2], 1'b1);
  FA fa_1 (.Cin(1'b1), .X(X[0]), .Y(xor_2_out), .S(S[0]), .Cout(fa_1_cout));
  FA fa_2 (.Cin(fa_1_cout), .X(X[1]), .Y(xor_3_out), .S(S[1]), .Cout(fa_2_cout));
  FA fa_3 (.Cin(fa_2_cout), .X(X[2]), .Y(xor_4_out), .S(S[2]), .Cout(fa_3_cout));
  FA fa_4 (.Cin(fa_3_cout), .X(X[3]), .Y(xor_1_out), .S(S[3]), .Cout(Bout));

  // Notes on the sheet:
  //   s0
  //   s1
  //   s2
  //   s3
endmodule
