// Logisim project banco_registradores.circ as structural Verilog: 1 circuit, main circuit main
module main (
  input  Reset,
  input  En_Reg0,
  input  En_Reg1,
  input  En_Reg2,
  input  En_Reg3,
  input  [3:0] DATA,
  input  En_Reg4,
  input  En_Reg5,
  input  En_Reg6,
  input  En_Reg_7,
  input  Clock,
  input  WRITE,
  output [3:0] Out_Reg0,
  output [3:0] Out_Reg1,
  output [3:0] Out_Reg2,
  output [3:0] Out_Reg3,
  output [3:0] Out_Reg4,
  output [3:0] Out_Reg5,
  output [3:0] Out_Reg6,
  output [3:0] Out_Reg7
);

  wire and_1_out, and_2_out, and_3_out, and_4_out, and_5_out, and_6_out, and_7_out, and_8_out, not_1_out;

  not not_1 (not_1_out, WRITE);
  and and_1 (and_1_out, not_1_out, En_Reg0);
  and and_2 (and_2_out, not_1_out, En_Reg1);
  and and_3 (and_3_out, En_Reg2, not_1_out);
  and and_4 (and_4_out, En_Reg3, not_1_out);
  and and_5 (and_5_out, En_Reg4, not_1_out);
  and and_6 (and_6_out, En_Reg5, not_1_out);
  and and_7 (and_7_out, En_Reg6, not_1_out);
  and and_8 (and_8_out, En_Reg_7, not_1_out);
  Register #(.width(4)) R0 (.D(DATA), .en(and_1_out), .Q(Out_Reg0), .clk(Clock), .clr(Reset));
  Register #(.width(4)) R2 (.D(DATA), .en(and_3_out), .Q(Out_Reg2), .clk(Clock), .clr(Reset));
  Register #(.width(4)) R4 (.D(DATA), .en(and_5_out), .Q(Out_Reg4), .clk(Clock), .clr(Reset));
  Register #(.width(4)) R6 (.D(DATA), .en(and_7_out), .Q(Out_Reg6), .clk(Clock), .clr(Reset));
  Register #(.width(4)) R1 (.D(DATA), .en(and_2_out), .Q(Out_Reg1), .clk(Clock), .clr(Reset));
  Register #(.width(4)) R3 (.D(DATA), .en(and_4_out), .Q(Out_Reg3), .clk(Clock), .clr(Reset));
  Register #(.width(4)) R5 (.D(DATA), .en(and_6_out), .Q(Out_Reg5), .clk(Clock), .clr(Reset));
  Register #(.width(4)) R7 (.D(DATA), .en(and_8_out), .Q(Out_Reg7), .clk(Clock), .clr(Reset));
endmodule
