// Logisim project contador.circ as structural Verilog: 1 circuit, main circuit main
module main (
  input  RESET,
  input  LOAD,
  input  ENABLE,
  input  CLOCK,
  input  [3:0] DATA,
  output [3:0] out_6
);

  wire and_1_out, and_2_out, multiplexer_1_out, multiplexer_2_out, multiplexer_3_out, multiplexer_4_out,
       xor_1_out, xor_2_out, xor_3_out, xor_4_out;

  xor xor_1 (xor_1_out, DATA[0], out_6[0]);
  T_Flip_Flop T0 (.clk(CLOCK), .T(multiplexer_1_out), .Q(out_6[0]), .reset(RESET), .en(ENABLE));  // open: Qn, preset
  Multiplexer multiplexer_1 (.in0(1'b1), .in1(xor_1_out), .out(multiplexer_1_out), .sel(LOAD));  // open: en
  xor xor_2 (xor_2_out, out_6[1], DATA[1]);
  T_Flip_Flop T1 (.clk(CLOCK), .T(multiplexer_2_out), .Q(out_6[1]), .reset(RESET), .en(ENABLE));  // open: Qn, preset
  Multiplexer multiplexer_2 (.in0(out_6[0]), .in1(xor_2_out), .out(multiplexer_2_out), .sel(LOAD));  // open: en
  xor xor_3 (xor_3_out, out_6[2], DATA[2]);
  and and_1 (and_1_out, out_6[0], out_6[1]);
  T_Flip_Flop T2 (.clk(CLOCK), .T(multiplexer_3_out), .Q(out_6[2]), .reset(RESET), .en(ENABLE));  // open: Qn, preset
  Multiplexer multiplexer_3 (.in0(and_1_out), .in1(xor_3_out), .out(multiplexer_3_out), .sel(LOAD));  // open: en
  and and_2 (and_2_out, and_1_out, out_6[2]);
  Multiplexer multiplexer_4 (.in0(and_2_out), .in1(xor_4_out), .out(multiplexer_4_out), .sel(LOAD));  // open: en
  xor xor_4 (xor_4_out, out_6[3], DATA[3]);
  T_Flip_Flop T3 (.clk(CLOCK), .T(multiplexer_4_out), .Q(out_6[3]), .reset(RESET), .en(ENABLE));  // open: Qn, preset
endmodule
