// Logisim project controle.circ as structural Verilog: 1 circuit, main circuit Controle
module Controle (
  input  Reset,
  input  Clock,
  input  OPCODE_2,
  input  OPCODE_1,
  input  OPCODE_0,
  input  Equal,
  output Out_WRITE,
  output Out_EN_PC,
  output Out_LOAD
);

  wire and_1_out, and_2_out, EN_BEQ_out, EN_BNE_out, EN_JMP_out, not_1_out, not_2_out, not_3_out, not_4_out,
       not_5_out, ST0_qn, ST1_q, ST1_qn;

  not not_1 (not_1_out, OPCODE_2);
  and and_1 (and_1_out, ST1_qn, OPCODE_2, ST0_qn);
  and and_2 (and_2_out, ST1_qn, not_1_out, ST0_qn);
  not not_2 (not_2_out, OPCODE_0);
  D_Flip_Flop ST1 (.clk(Clock), .D(and_1_out), .Q(ST1_q), .Qn(ST1_qn), .reset(Reset));  // open: preset, en
  not not_3 (not_3_out, OPCODE_0);
  not not_4 (not_4_out, OPCODE_1);
  not not_5 (not_5_out, Equal);
  D_Flip_Flop ST0 (.clk(Clock), .D(and_2_out), .Q(Out_WRITE), .Qn(ST0_qn), .reset(Reset));  // open: preset, en
  and EN_JMP (EN_JMP_out, OPCODE_2, ST1_q, not_3_out, not_4_out);
  and EN_BEQ (EN_BEQ_out, OPCODE_1, ST1_q, Equal, not_2_out, OPCODE_2);
  and EN_BNE (EN_BNE_out, not_5_out, not_4_out, OPCODE_2, ST1_q, OPCODE_1);
  or or_1 (Out_EN_PC, ST1_q, Out_WRITE);
  or or_2 (Out_LOAD, EN_JMP_out, EN_BEQ_out, EN_BNE_out);
endmodule
