// Logisim project decodificador.circ as structural Verilog: 1 circuit, main circuit DECODIFICADOR
module DECODIFICADOR (
  input  [2:0] SELECT,
  output D0,
  output D1,
  output D2,
  output D3,
  output D4,
  output D5,
  output D6,
  output D7
);

  wire not_1_out, not_2_out, not_3_out, not_4_out, not_5_out, not_6_out, not_7_out, not_8_out, not_9_out,
       not_10_out, not_11_out, not_12_out;

  not not_1 (not_1_out, SELECT[0]);
  not not_2 (not_2_out, SELECT[1]);
  not not_3 (not_3_out, SELECT[2]);
  not not_4 (not_4_out, SELECT[1]);
  not not_5 (not_5_out, SELECT[2]);
  not not_6 (not_6_out, SELECT[0]);
  not not_7 (not_7_out, SELECT[2]);
  not not_8 (not_8_out, SELECT[2]);
  not not_9 (not_9_out, SELECT[0]);
  not not_10 (not_10_out, SELECT[1]);
  not not_11 (not_11_out, SELECT[1]);
  not not_12 (not_12_out, SELECT[0]);
  and and_1 (D0, not_1_out, not_2_out, not_3_out);
  and and_2 (D1, SELECT[0], not_4_out, not_5_out);
  and and_3 (D2, not_6_out, SELECT[1], not_7_out);
  and and_4 (D3, SELECT[0], SELECT[1], not_8_out);
  and and_5 (D4, not_9_out, not_10_out, SELECT[2]);
  and and_6 (D5, SELECT[0], not_11_out, SELECT[2]);
  and and_7 (D6, not_12_out, SELECT[1], SELECT[2]);
  and and_8 (D7, SELECT[0], SELECT[1], SELECT[2]);
endmodule
