// Logisim project mini-arquitetura.circ as structural Verilog: 1 circuit, main circuit mini-arquitetura
module mini_arquitetura (
  input  RESET,
  output [2:0] RD,
  output [2:0] RF1,
  output [2:0] RF2,
  output [2:0] OPCODE
);

  wire BEQ_out, BNE_out, clock_1_out, decoder_1_out0, decoder_1_out1, decoder_1_out2, decoder_1_out3,
       decoder_1_out4, decoder_1_out5, decoder_1_out6, decoder_1_out7, JMP_out, not_1_out, not_2_out,
       not_3_out, not_4_out, not_5_out, not_6_out, not_7_out, or_1_out, ula_1_equal;
  wire [3:0] counter_1_q, multiplexer_1_out, multiplexer_2_out, multiplexer_3_out, R0_q, R1_q, R2_q, R3_q,
       R4_q, R5_q, R6_q, R7_q, ram_1_data, ula_1_resultado_op;

  not not_1 (not_1_out, or_1_out);
  Clock clock_1 (.out(clock_1_out));
  or or_1 (or_1_out, JMP_out, BEQ_out, BNE_out);
  and JMP (JMP_out, OPCODE[2], not_2_out, not_3_out);
  and BEQ (BEQ_out, ula_1_equal, OPCODE[2], OPCODE[1], not_4_out);
  and BNE (BNE_out, not_5_out, not_6_out, OPCODE[2], OPCODE[0]);
  Counter #(.width(4), .max('hf)) counter_1 (
    .load(or_1_out), .D(ram_1_data), .count(not_1_out), .Q(counter_1_q), .clk(clock_1_out), .clr(RESET));  // open: carry
  not not_2 (not_2_out, OPCODE[1]);
  not not_3 (not_3_out, OPCODE[0]);
  not not_4 (not_4_out, OPCODE[0]);
  not not_5 (not_5_out, ula_1_equal);
  not not_6 (not_6_out, OPCODE[1]);
  RAM #(.addrWidth(4), .dataWidth(16)) ram_1 (
    .addr(counter_1_q), .data({OPCODE, RD, RF1, RF2, ram_1_data}), .clk(clock_1_out));  // open: sel, ld, clr
  not not_7 (not_7_out, OPCODE[2]);
  ULA ula_1 (
    .IMEDIATO_000(ram_1_data), .ENTRADA_Y(multiplexer_3_out), .ENTRADA_X(multiplexer_1_out), .S1(OPCODE[1]),
    .S0(OPCODE[0]), .RESULTADO_OP(ula_1_resultado_op), .EQUAL(ula_1_equal));
  Decoder #(.select(3)) decoder_1 (
    .out0(decoder_1_out0), .out1(decoder_1_out1), .out2(decoder_1_out2), .out3(decoder_1_out3),
    .out4(decoder_1_out4), .out5(decoder_1_out5), .out6(decoder_1_out6), .out7(decoder_1_out7), .sel(RD));  // open: en
  Multiplexer #(.select(3), .width(4)) multiplexer_1 (
    .in0(R0_q), .in1(R1_q), .in2(R2_q), .in3(R3_q), .in4(R4_q), .in5(R5_q), .in6(R6_q), .in7(R7_q),
    .out(multiplexer_1_out), .sel(RF1));  // open: en
  Multiplexer #(.width(4)) multiplexer_2 (
    .in1(ula_1_resultado_op), .out(multiplexer_2_out), .sel(not_7_out), .en(1'b1));  // open: in0
  Multiplexer #(.select(3), .width(4)) multiplexer_3 (
    .in0(R0_q), .in1(R1_q), .in2(R2_q), .in3(R3_q), .in4(R4_q), .in5(R5_q), .in6(R6_q), .in7(R7_q),
    .out(multiplexer_3_out), .sel(RF2));  // open: en
  Register #(.width(4)) R0 (.D(multiplexer_2_out), .en(decoder_1_out0), .Q(R0_q), .clk(clock_1_out), .clr(RESET));
  Register #(.width(4)) R2 (.D(multiplexer_2_out), .en(decoder_1_out2), .Q(R2_q), .clk(clock_1_out), .clr(RESET));
  Register #(.width(4)) R4 (.D(multiplexer_2_out), .en(decoder_1_out4), .Q(R4_q), .clk(clock_1_out), .clr(RESET));
  Register #(.width(4)) R6 (.D(multiplexer_2_out), .en(decoder_1_out6), .Q(R6_q), .clk(clock_1_out), .clr(RESET));
  Register #(.width(4)) R1 (.D(multiplexer_2_out), .en(decoder_1_out1), .Q(R1_q), .clk(clock_1_out), .clr(RESET));
  Register #(.width(4)) R3 (.D(multiplexer_2_out), .en(decoder_1_out3), .Q(R3_q), .clk(clock_1_out), .clr(RESET));
  Register #(.width(4)) R5 (.D(multiplexer_2_out), .en(decoder_1_out5), .Q(R5_q), .clk(clock_1_out), .clr(RESET));
  Register #(.width(4)) R7 (.D(multiplexer_2_out), .en(decoder_1_out7), .Q(R7_q), .clk(clock_1_out), .clr(RESET));
endmodule
